# Fritzing sketch alt (saved by Fritzing 0.9.3b)
circuit board: 8.46667cm x 5.64444cm
breadboards: 1

parts:
  R1 = Resistor [tolerance=±5% resistance=330 package=THT]
  R2 = Resistor [tolerance=±5% resistance=330 package=THT]
  R3 = Resistor [tolerance=±5% resistance=330 package=THT]
  LED1 = RGB LED (com. cathode, rgb) [package="5 mm [THT]"]
  J1 = Piezo Speaker
  R6 = Basic Flex Resistor
  U2 = POT [package=alps_pot]
  R5 = Resistor [tolerance=±5% resistance=10k package=THT]
  R7 = Resistor [tolerance=±5% resistance=5k package=THT]
  Part1 = Arduino Uno (Rev3)

nets:
  N1: R1.Pin_0, Part1.D11_PWM/MOSI
  N2: R1.Pin_1, LED1.red_anode
  N3: R2.Pin_0, Part1.D9_PWM
  N4: R2.Pin_1, LED1.blue_anode
  N5: R3.Pin_0, Part1.D10_PWM/SS
  N6: R3.Pin_1, LED1.green_anode
  N7: LED1.common_cathode, J1.pin1, R6.Pin_2, U2.A, R7.Pin_0, Part1.GND
  N8: J1.pin2, Part1.D3_PWM
  N9: R6.pin_1, R5.Pin_0, Part1.A1
  N10: U2.E, R5.Pin_1, Part1.5V
  N11: U2.S, R7.Pin_1, Part1.A0

// code stored in the sketch: Discoteca.ino
// some constants for abstraction and readability
const int softPot = A0;
const int flexSensor = A1;
const int buzzerPin = 3;
const int blueLed = 9;
const int greenLed = 10;
const int redLed = 11;

// tempo is constant, and is an empirical obtained value
const int tempo = 113;

void setup()
{ 
  pinMode(buzzerPin, OUTPUT);
  pinMode(redLed, OUTPUT);
  pinMode(blueLed, OUTPUT);
  pinMode(greenLed, OUTPUT);
}

void loop()
{
  int beats;
  int flexVal;
  int softPotVal;
  int note;
  
  // colors is an array of three integers, interpret as following:
  // - colors[i] = 1 if we want to light the LED related to i ON
  // i = 0 is red, i = 1 is green, i = 2 is blue
  int colors[3];

  // a list of notes is just an array of characters
  // interpret each character as a note
  char notesList[] = {'a','b','c','C','d','e','f','g', ' '};
  const int numNotes = 9;

  // read the sensors
  softPotVal = analogRead(softPot);
  flexVal = analogRead(flexSensor);

  // beats is a function of the flex sensor
  switch(flexVal)
  {
    case 711 ... 800:
      beats = 1;
      break;
    case 680 ... 710:
      beats = 4;
      break;
    default:
      beats = 8;
      break;
  }
 
  // the notes are in function of the reading on the soft pot
  // also the colors match the notes
  switch(softPotVal)
  {
    case 0 ... 127:
      note = pickRandomNote(notesList, numNotes);

      // do not turn the leds on when note means stop
      if (note == ' ')
      {   
        colors[0] = 0;
        colors[1] = 0;
        colors[2] = 0;        
      }
      else
      {
        // if we succesfully get a note, pick a color at random that is not 000
        do
        {
          colors[0] = random(0, 2);
          colors[1] = random(0, 2);
          colors[2] = random(0, 2);     
        } while ((colors[0] == 0) &&
                 (colors[1] == 0) &&
                 (colors[2] == 0));
      }
      break;

     case 128 ... 254:
      note = 'b';
      colors[0] = 0;
      colors[1] = 0;
      colors[2] = 1;
      break;
      
     case 255 ... 381:
      note = 'c';
      colors[0] = 0;
      colors[1] = 1;
      colors[2] = 0;
      break;
      
     case 382 ... 508:
      note = 'C';
      colors[0] = 0;
      colors[1] = 1;
      colors[2] = 1;
      break;
      
     case 509 ... 635:
      note = 'd';
      colors[0] = 1;
      colors[1] = 0;
      colors[2] = 0;
      break;
      
     case 636 ... 762:
      note = 'e';
      colors[0] = 1;
      colors[1] = 0;
      colors[2] = 1;
      break;
      
     case 763 ... 889:
      note = 'f';
      colors[0] = 1;
      colors[1] = 1;
      colors[2] = 0;
      break;
      
     default:
      note = 'g';
      colors[0] = 1;
      colors[1] = 1;
      colors[2] = 1;
      break;
  }

  // play the buzzer
  tone(buzzerPin, frequency(note, numNotes), beats * tempo);

  // lights blink along with the buzzer
  blinkLights(colors, beats * tempo);
  
  // this is also taken empirically
  delay(beats * tempo / 5);
}

// this function takes an array of colors and the speed in which to blink
// then makes the RGB Led blink as the parameters specify
void blinkLights(int colors[], int vel)
{
  digitalWrite(redLed, colors[0]);
  digitalWrite(greenLed, colors[1]);
  digitalWrite(blueLed, colors[2]);
  delay(vel / 2);
  digitalWrite(redLed, LOW);
  digitalWrite(blueLed, LOW);
  digitalWrite(greenLed, LOW);
  delay(vel / 2);
}

// this function takes a note and assigns to it a frequency
// thanks to the SIK guide for this piece of code
int frequency(char note, int numNotes) 
{
  int i;
  
  // these are the notes 
  char notesList[numNotes] = { 
    'c', 'd', 'e', 'f', 'g', 'a', 'b', 'C'    };

  // frequency[i] matches names[i]
  int frequencies[numNotes] = {
    262, 294, 330, 349, 392, 440, 494, 523    };

  // Now we'll search through the letters in the array, and if
  // we find it, we'll return the frequency for that note.
  for (i = 0; i < numNotes; i++)  // Step through the notes
  {
    if (notesList[i] == note)         // Is this the one?
    {
      return(frequencies[i]);     // Yes! Return the frequency and exit function.
    }
  }
  return 0;  // We looked through everything and didn't find it,
  // but we still need to return a value, so return 0.
}

char pickRandomNote(char notes[], int numNotes)
{
  return notes[random(0, numNotes)];  
}
