# Fritzing sketch pcb (saved by Fritzing 0.9.3b)
circuit board: 12.1215cm x 9.36725cm
breadboards: 1

parts:
  J2 = Piezo Speaker
  R8 = Resistor [tolerance=±5% resistance=330 package=THT]
  R9 = Resistor [tolerance=±5% resistance=330 package=THT]
  R10 = Resistor [tolerance=±5% resistance=330 package=THT]
  R11 = Resistor [tolerance=±5% resistance=5k package=THT]
  U4 = POT [package=pot_alpha_rv16af-20]
  HEF2 = HEF4094 [package="DIP16 [THT]"]
  LED3 = LED - 5mm [color="Red (633nm)" package="5 mm [THT]"]
  LED5 = LED - 5mm [color="Yellow (595nm)" package="5 mm [THT]"]
  LED6 = LED - 5mm [color="Yellow (595nm)" package="5 mm [THT]"]
  LED7 = LED - 5mm [color="Green (555nm)" package="5 mm [THT]"]
  LED8 = LED - 5mm [color="Green (555nm)" package="5 mm [THT]"]
  LED9 = LED - 5mm [color="Blue (430nm)" package="5 mm [THT]"]
  LED10 = LED - 5mm [color="Blue (430nm)" package="5 mm [THT]"]
  R16 = Resistor [tolerance=±5% resistance=330 package=THT]
  R17 = Resistor [tolerance=±5% resistance=330 package=THT]
  R18 = Resistor [tolerance=±5% resistance=330 package=THT]
  R19 = Resistor [tolerance=±5% resistance=330 package=THT]
  R20 = Resistor [tolerance=±5% resistance=330 package=THT]
  R21 = Resistor [tolerance=±5% resistance=330 package=THT]
  R22 = Resistor [tolerance=±5% resistance=330 package=THT]
  R24 = Resistor [tolerance=±5% resistance=220 package=THT]
  Arduino = Arduino Uno (Rev3)
  SparkFun1 = SoftPot Membrane Potentiometer - 50mm [part_number=SEN-08680]
  R12 = Resistor [tolerance=±5% resistance=10k package=THT]
  U5 = LCD-16X2 [package=lcd-16x2]
  LED4 = LED - 5mm [color="Red (633nm)" package="5 mm [THT]"]
  R7 = Basic Flex Resistor
  LED2 = RGB LED (com. cathode, rgb) [package="5 mm [THT]"]

nets:
  VSS: J2.pin1, R11.Pin_0, U4.E, HEF2.Vss, HEF2.Q6, R16.Pin_1, R17.Pin_1, R18.Pin_1, R19.Pin_1, R20.Pin_1, R21.Pin_1, R22.Pin_1, R24.Pin_1, Arduino.GND, SparkFun1.leg1, U5.VSS, U5.R_W, U5.K, R7.Pin_2, LED2.common_cathode
  N1: J2.pin2, Arduino.D8
  N2: R8.Pin_0, Arduino.A2
  N3: R8.Pin_1, LED2.red_anode
  N4: R9.Pin_0, Arduino.D10_PWM/SS
  N5: R9.Pin_1, LED2.green_anode
  N6: R10.Pin_0, Arduino.D9_PWM
  N7: R10.Pin_1, LED2.blue_anode
  N8: R11.Pin_1, Arduino.A0, SparkFun1.wiper
  VDD: U4.A, HEF2.Q's, HEF2.Vdd, Arduino.5V, SparkFun1.leg2, R12.Pin_1, U5.VDD, U5.A
  N9: U4.S, U5.VO
  N10: HEF2.STROBE, LED4.anode
  N11: HEF2.DATA, LED5.anode
  N12: HEF2.CLOCK, LED6.anode
  N13: HEF2.Q1, LED7.anode
  N14: HEF2.Q2, LED8.anode
  N15: HEF2.Q3, LED9.anode
  N16: HEF2.Q4, LED10.anode
  N17: HEF2.Q8, Arduino.D3_PWM
  N18: HEF2.Q7, Arduino.D4
  N19: HEF2.Q5, Arduino.D2
  N20: HEF2.OE, LED3.anode
  N21: LED3.cathode, R16.Pin_0
  N22: LED5.cathode, R18.Pin_0
  N23: LED6.cathode, R19.Pin_0
  N24: LED7.cathode, R20.Pin_0
  N25: LED8.cathode, R21.Pin_0
  N26: LED9.cathode, R22.Pin_0
  N27: LED10.cathode, R24.Pin_0
  N28: R17.Pin_0, LED4.cathode
  N29: Arduino.A1, R12.Pin_0, R7.pin_1
  N30: Arduino.D11_PWM/MOSI, U5.RS
  N31: Arduino.D12/MISO, U5.DB4
  N32: Arduino.D13/SCK, U5.E
  N33: Arduino.D5_PWM, U5.DB7
  N34: Arduino.D6_PWM, U5.DB6
  N35: Arduino.D7, U5.DB5

custom parts:
  SoftPot Membrane Potentiometer - 50mm: These are very thin variable potentiometers. By pressing down on various parts of the strip, the resistance linearly changes from 100Ohms to 10,000Ohms allowing the user to very accurately calculate the relative position on the strip. Can be used as an accurate positional indicator for CNC head positioning, variable user input (volume level input for example), straight user input (multiple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

// code stored in the sketch: Discoteca2.0.ino
/*
 * Name: Rafael Antonio Laya Alfonzo
 * November 2017
 * Class: ENGR 102 intro to electronics (Fall 2017)
 * Software Version: Arduino 1.8.2
 * Source code for Discoteca 2.0 more information on the report
 * The reader can use this code as they please but I won't be liable of anything
*/


#include <LiquidCrystal.h>
LiquidCrystal lcd(11, 13, 12, 7, 6, 5);

// some constants for abstraction and readability
const int softPot = A0;
const int flexSensor = A1;
const int buzzerPin = 8;
const int blueLed = 9;
const int greenLed = 10;
const int redLed = 16;
const int numLeds = 8;

int dataPin = 2; 
int clockPin = 3;
int latchPin = 4;

byte data = 0;

// tempo is constant, and is an empirical obtained value
const int tempo = 113;

void setup()
{
  Serial.begin(9600);
  pinMode(buzzerPin, OUTPUT);
  pinMode(redLed, OUTPUT);
  pinMode(blueLed, OUTPUT);
  pinMode(greenLed, OUTPUT);

  pinMode(dataPin, OUTPUT);
  pinMode(clockPin, OUTPUT);  
  pinMode(latchPin, OUTPUT);


  lcd.begin(16, 2); //Initialize the 16x2 LCD


  lcd.clear();  //Clear any old data displayed on the LCD
}

void loop()
{
  int beats;
  int flexVal;
  int softPotVal;
  int note; 

  // colors is an array of three integers, interpret as following:
  // - colors[i] = 1 if we want to light the LED related to i ON
  // i = 0 is red, i = 1 is green, i = 2 is blue
  int colors[3];

  // a list of notes is just an array of characters
  // interpret each character as a note
  char notesList[] = {'a', 'b', 'c', 'C', 'd', 'e', 'f', 'g', ' '};
  const int numNotes = 9;

  // read the sensors
  softPotVal = analogRead(softPot);
  flexVal = analogRead(flexSensor);

  Serial.println(flexVal);
  
  // beats is a function of the flex sensor
  switch (flexVal)
  {
    case 800 ... 900:
      beats = 1;
      break;
    case 720 ... 799:
      beats = 4;
      break;
    default:
      beats = 8;
      break;
  }

  Serial.println(softPotVal);
  // the notes are in function of the reading on the soft pot
  // also the colors match the notes
  switch (softPotVal)
  {
    case 0 ... 49:
      note = pickRandomNote(notesList, numNotes);

      // do not turn the leds on when note means stop
      if (note == ' ')
      {
        colors[0] = 0;
        colors[1] = 0;
        colors[2] = 0;
      }
      else
      {
        // if we succesfully get a note, pick a color at random that is not 000
        do
        {
          colors[0] = random(0, 2);
          colors[1] = random(0, 2);
          colors[2] = random(0, 2);
        } while ((colors[0] == 0) &&
                 (colors[1] == 0) &&
                 (colors[2] == 0));
      }
      break;

    case 50 ... 140:
      note = 'c';
      colors[0] = 0;
      colors[1] = 0;
      colors[2] = 1;
    break;

    case 141 ... 254:
      note = 'd';
      colors[0] = 0;
      colors[1] = 0;
      colors[2] = 1;
      break;

    case 255 ... 381:
      note = 'e';
      colors[0] = 0;
      colors[1] = 1;
      colors[2] = 0;
      break;

    case 382 ... 508:
      note = 'f';
      colors[0] = 0;
      colors[1] = 1;
      colors[2] = 1;
      break;

    case 509 ... 635:
      note = 'g';
      colors[0] = 1;
      colors[1] = 0;
      colors[2] = 0;
      break;

    case 636 ... 762:
      note = 'a';
      colors[0] = 1;
      colors[1] = 0;
      colors[2] = 1;
      break;

    case 763 ... 889:
      note = 'b';
      colors[0] = 1;
      colors[1] = 1;
      colors[2] = 0;
      break;

    default:
      note = 'C';
      colors[0] = 1;
      colors[1] = 1;
      colors[2] = 1;
      break;
  }

  printOnLCD(note, frequency(note, numNotes), beats);
  
  // play the buzzer
  tone(buzzerPin, frequency(note, numNotes), beats * tempo);

  // lights blink along with the buzzer
  blinkLightsON(colors, beats * tempo);

  // LEDs dance along with the frequency of the music
  danceLeds(note);

  delay(beats * tempo / 2);

  blinkLightsOFF();

  delay(beats * tempo / 2);

  // this is also taken empirically
  delay(beats * tempo / 5);
}

void blinkLightsOFF()
{
  digitalWrite(redLed, LOW);
  digitalWrite(blueLed, LOW);
  digitalWrite(greenLed, LOW);
}

void blinkLedsOFF()
{
  for(int i = 0; i < 8; i++)
  {
    shiftWrite(i, LOW);
  }
}

// this function takes an array of colors and the speed in which to blink
// then makes the RGB Led blink as the parameters specify
void blinkLightsON(int colors[], int vel)
{
  digitalWrite(redLed, colors[0]);
  digitalWrite(greenLed, colors[1]);
  digitalWrite(blueLed, colors[2]);
}

// this function takes a note and assigns to it a frequency
// thanks to the SIK guide for this piece of code
int frequency(char note, int numNotes)
{
  int i;

  // these are the notes
  char notesList[numNotes] = {
    'c', 'd', 'e', 'f', 'g', 'a', 'b', 'C'};

  // frequency[i] matches names[i]
  int frequencies[numNotes] = {
    262, 294, 330, 349, 392, 440, 494, 523};

  // Now we'll search through the letters in the array, and if
  // we find it, we'll return the frequency for that note.
  for (i = 0; i < numNotes; i++)  // Step through the notes
  {
    if (notesList[i] == note)         // Is this the one?
    {
      return (frequencies[i]);    // Yes! Return the frequency and exit function.
    }
  }
  return 0;  // We looked through everything and didn't find it,
  // but we still need to return a value, so return 0.
}

char pickRandomNote(char notes[], int numNotes)
{
  return notes[random(0, numNotes)];
}

void shiftWrite(int desiredPin, boolean desiredState)
{
  //Serial.println(data);
  bitWrite(data, desiredPin, desiredState);
  //Serial.println(data);
  shiftOut(dataPin, clockPin, MSBFIRST, data);

  digitalWrite(latchPin, HIGH);
  digitalWrite(latchPin, LOW);
}

void danceLeds(char note)
{
  Serial.println(note);

  for(int index = 0; index < numLeds; index++)
  {
    Serial.println(noteValue(note, 8));
    if(shouldBlink(numLeds - 1 - index, noteValue(note, 8)))
    {
      shiftWrite(numLeds - 1 - index, HIGH);
    }
    else
    {
      shiftWrite(numLeds - 1 - index, LOW);
    }
  }
}

boolean shouldBlink(int LED, int noteValue)
{
  return (LED >= noteValue);
}

int noteValue(char note, int numNotes)
{
  if (note == ' ')
  {
    return numNotes + 100;
  }
  
  char notesList[numNotes] = {
    'c', 'd', 'e', 'f', 'g', 'a', 'b', 'C'};

  for(int i = 0; i < 8; i++)
  {
    if (notesList[i] == note)
    {
      return i;
    }
    else
    {
      continue;
    }
  }

  return 0;
}

void printOnLCD(int note,int frequency,int beats)
{
  lcd.clear();
  lcd.setCursor(0, 0);
  lcd.print("Note: ");
  lcd.print(char(note));
  lcd.print("  Hz: ");
  lcd.print(frequency);
  lcd.setCursor(0, 1);
  lcd.print("Speed: ");

  int speedLevel;
  if(beats == 1)
  {
     speedLevel = 3;
  }
  else if (beats == 4)
  {
    speedLevel = 2;
  }
  else
  {
    speedLevel = 1;
  }
  lcd.print(speedLevel);
}
