# Fritzing sketch pcb (saved by Fritzing 0.9.3b)
circuit board: 7.76511cm x 9.10159cm
breadboards: 1

parts:
  Buzzer = Piezo Speaker
  Matrix_keypad1 = KEYPAD 4x4
  header = Header 12 [package=1x12_machine-pin-header_lock.004]
  R4 = Resistor [tolerance=±5% resistance=10k package="2010 [SMD]"]
  R3 = Resistor [tolerance=±5% resistance=10k package="2010 [SMD]"]
  R5 = Resistor [tolerance=±5% resistance=330 package="2010 [SMD]"]
  R6 = Resistor [tolerance=±5% resistance=330 package="2010 [SMD]"]
  Servo = Basic Servo
  Laser = LD
  PhotoRes2 = PHOTOCELL [package=photocell-kit]
  LED1 = RGB LED (com. anode, rbg) [package="5 mm [THT]"]
  PhotoRes1 = PHOTOCELL [package=photocell-kit]
  Arduino = Arduino Uno (Rev3)

nets:
  N1: Buzzer.pin1, R4.Pin_1, R3.Pin_1, PhotoRes2.P$2, LED1.common_anode, Arduino.GND
  N2: Buzzer.pin2, Arduino.D11_PWM/MOSI
  N3: Matrix_keypad1.col1, header.8, Arduino.D9_PWM
  N4: Matrix_keypad1.col2, header.7, Arduino.D8
  N5: Matrix_keypad1.col3, header.6, Arduino.D7
  N6: Matrix_keypad1.col4, header.5, Arduino.D6_PWM
  N7: Matrix_keypad1.row1, header.4, Arduino.D5_PWM
  N8: Matrix_keypad1.row2, header.3, Arduino.D4
  N9: Matrix_keypad1.row3, header.2, Arduino.D3_PWM
  N10: Matrix_keypad1.row4, header.1, Arduino.D2
  N11: R4.Pin_0, PhotoRes1.P$1, Arduino.A0
  N12: R3.Pin_0, PhotoRes2.P$1, Arduino.A1
  N13: R5.Pin_0, LED1.red_cathode
  N14: R5.Pin_1, Arduino.D13/SCK
  N15: R6.Pin_0, LED1.green_cathode
  N16: R6.Pin_1, Arduino.D12/MISO
  N17: Servo.gnd, Laser.cathode
  N18: Servo.vcc, Laser.anode
  N19: Servo.pulse, Arduino.D10_PWM/SS
  N20: PhotoRes1.P$2, Arduino.5V

custom parts:
  KEYPAD 4x4: Matrix keypad 16 buttons, 4 rows x 4 columns
  LD: A Generic Red Dot Laser Diode Module (~5mW)
