# Fritzing sketch Frizting - SpeedyBlinker (saved by Fritzing 0.9.3b)
circuit board: 8.46667cm x 5.64444cm
breadboards: 1

parts:
  Part1 = Arduino Uno (Rev3)
  LED1 = smd LED [color="Red (633nm)" package="1206 [SMD]"]
  R1 = Resistor [tolerance=±5% resistance=220 package=THT]
  R2 = Resistor [tolerance=±5% resistance=220 package=THT]
  S1 = Pushbutton [package="[THT]"]

nets:
  N1: Part1.D12/MISO, R2.Pin_0, S1.Pin_3, S1.Pin_4
  N2: Part1.D13/SCK, LED1.anode
  N3: Part1.GND, R1.Pin_0, R2.Pin_1
  N4: Part1.5V, S1.Pin_1, S1.Pin_2
  N5: LED1.cathode, R1.Pin_1

// code stored in the sketch: 1stled.ino
 /*
 * Rafael Laya
 * Professor Basham's ENGR102 class at Shoreline Community College
 * The reader can use this code as they please but I won't be liable of anything
 * 
 * Purpose and usage:
 * Blinks an LED connected to pin 13
 * while varying the duration of on/off time
 * when user presses the button serial monitor will output the result
 * for re-testing just press the button again (or you can also press the arduino reset button)
 */

// Set up some constants for abstraction and portability of the code
const int redLed = 13;
const int pushButton = 12;

int buttonState;

void setup() {
  pinMode(redLed, OUTPUT);
  pinMode(pushButton, INPUT);
  buttonState = 0;

  // getting serial monitor ready for user interaction purposes
  Serial.begin(9600);
  Serial.println("********************** Serial monitor has just been initiated **********************");
}

void loop() {
  
  delay(1000);
  
  // advise the user the test has begun
  Serial.println("New Test initiated");

  // try from 1ms up to 100ms delay in steps of one
  for(int delayTime = 1; delayTime <= 100; delayTime++)
  { 
    // blink 149 times during each try
    for(int k = 0; k <= 149; k++)
    {
      buttonState = digitalRead(pushButton);
      blinkRedLed(delayTime);

      // when the user decides he can see the LED blinking he'll push the button
      if (buttonState == HIGH)
      {
        // output the results
        Serial.print("You cann see the blinking light when it blinks every ");
        Serial.print(delayTime);
        Serial.println(" milliseconds");
        testEnded();
        return;
      }
    }
  }
  // wait 5 seconds before re-testing (in case the user never pressed the button)
  delay(5000);
}

void blinkRedLed(int delayTime)
{
  digitalWrite(redLed, HIGH);
  delay(delayTime);
  digitalWrite(redLed, LOW);
  delay(delayTime);  
}

void testEnded(void)
{
  delay(1000);

  /* 
   *  user will press the button after the test has ended
   *  if it is the case that he wants to take another test
   */
  
  while (true)
  {
    buttonState = digitalRead(pushButton);
    if (buttonState == HIGH)
    {
      buttonState = 0;
      break;
    }
    else
    {
      continue;
    }
  }
  return;
}
